// Logisim project Portas Lógicas - 1.circ as structural Verilog: 1 circuit, main circuit main
module main (
  input  A,
  input  A_2,
  input  B,
  input  B_2,
  input  C,
  input  C_2,
  input  D,
  input  A_3,
  input  A_4,
  input  B_3,
  input  B_4,
  input  C_3,
  input  D_2,
  output S,
  output S_2,
  output S_3,
  output out_17
);

  wire and_1_out, and_2_out, and_3_out, and_4_out, nand_2_out, not_1_out, not_2_out, or_3_out, xor_1_out,
       xor_2_out;

  and and_1 (and_1_out, A_2, B_2);
  not not_1 (not_1_out, B_4);
  or or_1 (S, and_1_out, C_2);
  and and_2 (and_2_out, A_4, not_1_out);
  and and_3 (and_3_out, B_4, ~A_4);  // AND_Gate
  or or_2 (S_3, A_4, and_2_out, and_3_out);
  and and_4 (and_4_out, A, B);
  xor xor_1 (xor_1_out, C, D);
  nand nand_1 (S_2, ~and_4_out, xor_1_out);  // NAND_Gate
  not not_2 (not_2_out, C_3);
  or or_3 (or_3_out, A_3, ~B_3);  // OR_Gate
  xor xor_2 (xor_2_out, B_3, not_2_out);
  nand nand_2 (nand_2_out, ~or_3_out, xor_2_out, D_2);  // NAND_Gate
  nor nor_1 (out_17, nand_2_out, D_2);

  // Notes on the sheet:
  //   1)
  //   3)
  //   A . B
  //   C
  //   (A . B) + C
  //   2)
  //   _
  //   A + AB + AB
  //   4)
  //   _
  //   A . B
  //   ___
  //   A . B
  //   __
  //   C |+| D
  //   __
  //   _____________
  //   ___
  //   __
  //   (C |+| D)
  //   __
  //   (A . B) . 
  //   _______________
  //   ____
  //   _
  //   ___________________
  //   _
  //   __
  //   |  |
  //   {(A + B) . (B + C) . D} + D
  //   __
endmodule
