// Logisim project circuito.circ as structural Verilog: 2 circuits, main circuit main
module main (
  input  A,
  input  B,
  input  C
);

  wire bcd_7_seg_1_a_2, bcd_7_seg_1_b_2, bcd_7_seg_1_c_2, bcd_7_seg_1_d, bcd_7_seg_1_e, bcd_7_seg_1_f,
       bcd_7_seg_1_g;

  BCD_7_SEG bcd_7_seg_1 (
    .a_2(bcd_7_seg_1_a_2), .b_2(bcd_7_seg_1_b_2), .c_2(bcd_7_seg_1_c_2), .d(bcd_7_seg_1_d),
    .e(bcd_7_seg_1_e), .f(bcd_7_seg_1_f), .g(bcd_7_seg_1_g), .A(A), .B(B), .C(C));
  _7_Segment_Display u_7_segment_display_1 (
    .g(bcd_7_seg_1_g), .f(bcd_7_seg_1_f), .a(bcd_7_seg_1_a_2), .b(bcd_7_seg_1_b_2), .e(bcd_7_seg_1_e),
    .d(bcd_7_seg_1_d), .c(bcd_7_seg_1_c_2));  // open: dp
endmodule

// 7 SEG
module BCD_7_SEG (
  input  A,
  input  B,
  input  C,
  output a_2,
  output b_2,
  output c_2,
  output d,
  output e,
  output f,
  output g
);

  wire and_1_out;

  and and_1 (and_1_out, ~A, ~B);  // AND_Gate
  or or_1 (a_2, and_1_out, C);
  or or_2 (b_2, B, ~C);  // OR_Gate
  or or_3 (c_2, B, ~C);  // OR_Gate
  or or_4 (d, A, C);
  or or_5 (e, ~B, C);  // OR_Gate
  or or_6 (f, ~B, C);  // OR_Gate
  and and_2 (g, ~A, ~B);  // AND_Gate
endmodule
