// Logisim project exercicios-23-08-22.circ as structural Verilog: 1 circuit, main circuit main
module main (
  input  A,
  input  B,
  input  A_2,
  input  C,
  input  B_2,
  input  A_3,
  input  A_4,
  input  B_3,
  input  B_4,
  input  C_2,
  input  C_3,
  input  A_5,
  input  B_5,
  input  A_6,
  input  C_4,
  input  B_6,
  input  C_5,
  input  D,
  input  A_7,
  input  A_8,
  input  B_7,
  input  B_8,
  input  C_6,
  input  C_7,
  output S,
  output S_2,
  output out_27,
  output S_3,
  output S_4,
  output S_5,
  output S_6,
  output out_32
);

  wire and_1_out, and_4_out, and_6_out, and_7_out, and_8_out, and_9_out, and_10_out, and_11_out, and_12_out,
       and_13_out, and_14_out, nand_1_out, nor_1_out, nor_3_out, nor_4_out, not_1_out, not_2_out, not_3_out,
       not_4_out, not_5_out, not_6_out, not_7_out, not_8_out, not_9_out, not_10_out, not_11_out, not_12_out,
       not_13_out, not_14_out, or_1_out, or_2_out, or_3_out, xor_1_out, xor_2_out;

  and and_1 (and_1_out, A_6, B_6);
  nor nor_1 (nor_1_out, A, B);
  nand nand_1 (nand_1_out, A_4, B_4);
  not not_1 (not_1_out, D);
  nand nand_2 (S, nor_1_out, C);
  nor nor_2 (S_3, nand_1_out, C_3);
  nor nor_3 (nor_3_out, and_1_out, C_5);
  and and_2 (S_5, nor_3_out, not_1_out);
  not not_2 (not_2_out, A_2);
  not not_3 (not_3_out, B_2);
  or or_1 (or_1_out, not_2_out, not_3_out);
  not not_4 (not_4_out, A_5);
  xor xor_1 (xor_1_out, A_5, B_5);
  not not_5 (not_5_out, A_7);
  xor xor_2 (xor_2_out, A_7, B_7);
  not not_6 (not_6_out, B_7);
  nor nor_4 (nor_4_out, not_2_out, not_3_out);
  or or_2 (or_2_out, not_4_out, xor_1_out);
  not not_7 (not_7_out, C_4);
  or or_3 (or_3_out, xor_2_out, not_6_out);
  not not_8 (not_8_out, C_6);
  and and_3 (S_2, or_1_out, nor_4_out);
  and and_4 (and_4_out, not_5_out, or_3_out);
  and and_5 (S_4, or_2_out, not_7_out);
  or or_4 (S_6, and_4_out, not_8_out);
  not not_9 (not_9_out, A_3);
  not not_10 (not_10_out, B_3);
  not not_11 (not_11_out, C_2);
  not not_12 (not_12_out, A_8);
  not not_13 (not_13_out, B_8);
  not not_14 (not_14_out, C_7);
  and and_6 (and_6_out, not_9_out, not_10_out, C_2);
  and and_7 (and_7_out, A_3, not_10_out, not_11_out);
  and and_8 (and_8_out, A_3, not_10_out, C_2);
  and and_9 (and_9_out, not_12_out, not_13_out, C_7);
  and and_10 (and_10_out, not_12_out, B_8, not_14_out);
  and and_11 (and_11_out, not_12_out, B_8, C_7);
  and and_12 (and_12_out, A_8, not_13_out, not_14_out);
  and and_13 (and_13_out, A_8, B_8, not_14_out);
  and and_14 (and_14_out, A_8, B_8, C_7);
  or or_5 (out_27, and_6_out, and_7_out, and_8_out);
  or or_6 (out_32, and_9_out, and_10_out, and_11_out, and_12_out, and_13_out, and_14_out);
endmodule
