// Digital circuit teste.dig as structural Verilog
module teste (
  input  A,
  input  B,
  input  C,
  input  A_2,
  input  B_2,
  input  S,
  output Y,
  output C_2
);

  wire and_1_out, and_2_out, and_3_out, and_4_out;

  and and_1 (and_1_out, A, B);
  and and_2 (and_2_out, ~A, ~B, C);  // And
  or or_1 (Y, and_1_out, and_2_out);
  and and_3 (and_3_out, A_2, ~S);  // And
  and and_4 (and_4_out, S, B_2);
  or or_2 (C_2, and_3_out, and_4_out);

  // Notes on the sheet:
  //   Questão 02
  //   Questão 03
endmodule
